// Logisim project SoCIN.circ as structural Verilog: 21 circuits, main circuit ParIS
module ParIS (
  input  in_1,
  input  [9:0] in_2,
  input  in_3,
  input  in_4,
  input  in_5,
  input  [9:0] in_6,
  input  in_7,
  input  in_8,
  input  in_9,
  input  in_10,
  input  [9:0] in_11,
  input  in_12,
  input  in_13,
  input  [9:0] in_14,
  input  in_15,
  input  [9:0] in_16,
  output out_17,
  output [9:0] out_18,
  output out_19,
  output out_20,
  output [9:0] out_21,
  output out_22,
  output out_23,
  output [9:0] out_24,
  output out_25,
  output out_26,
  output [9:0] out_27,
  output out_28,
  output out_29,
  output [9:0] out_30,
  output out_31
);

  wire CLK, EgntL, EgntN, EgntS, EgntW, Eidle, Erd, Erok, LgntE, LgntN, LgntS, LgntW, Lidle, Lrd, Lrok,
       NgntE, NgntL, NgntS, NgntW, Nidle, Nrd, Nrok, SgntE, SgntL, SgntN, SgntW, Sidle, Srd, Srok, WgntE,
       WgntL, WgntN, WgntS, Widle, Wrd, Wrok;
  wire [2:0] Local_In_x_reqw;
  wire [3:0] Local_In_x_reqe, Local_In_x_reqn, Local_In_x_reqs, North_In_x_reql;
  wire [9:0] Edata, Ldata, Ndata, Sdata, Wdata;

  Clock clock_1 (.out(CLK));
  Xin Local_In (
    .in_data(in_2), .FC_TYPE(in_9), .in_val(in_1), .x_gnt({WgntL, SgntL, EgntL, NgntL}), .x_Sidle(Sidle),
    .x_rd({Wrd, Srd, Erd, Nrd}), .x_Eidle(Eidle), .x_Nidle(Nidle), .x_Lidle(Lidle), .x_Widle(Widle),
    .CLK(CLK), .RST(in_3), .ROUTING_TYPE(in_7), .FIFO_TYPE(in_4), .WF_TYPE(in_8), .x_dout(Ldata),
    .x_rok(Lrok), .in_ret(out_17), .x_reqN(Local_In_x_reqn[0]), .x_reqE(Local_In_x_reqe[0]),
    .x_reqS(Local_In_x_reqs[0]), .x_reqW(Local_In_x_reqw[0]));  // open: x_reqL
  Xin North_In (
    .in_data(in_6), .FC_TYPE(in_9), .in_val(in_5), .x_gnt({WgntN, SgntN, EgntN, LgntN}), .x_Sidle(Sidle),
    .x_rd({Wrd, Srd, Erd, Lrd}), .x_Eidle(Eidle), .x_Nidle(Nidle), .x_Lidle(Lidle), .x_Widle(Widle),
    .CLK(CLK), .RST(in_3), .ROUTING_TYPE(in_7), .FIFO_TYPE(in_4), .WF_TYPE(in_8), .x_dout(Ndata),
    .x_rok(Nrok), .x_reqL(North_In_x_reql[0]), .in_ret(out_20), .x_reqS(Local_In_x_reqs[1]));  // open: x_reqN, x_reqE, x_reqW
  Xin East_In (
    .in_data(in_14), .FC_TYPE(in_9), .in_val(in_13), .x_gnt({WgntE, 2'b00, LgntE}), .x_Sidle(Sidle),
    .x_rd({Wrd, Srd, Nrd, Lrd}), .x_Eidle(Eidle), .x_Nidle(Nidle), .x_Lidle(Lidle), .x_Widle(Widle),
    .CLK(CLK), .RST(in_3), .ROUTING_TYPE(in_7), .FIFO_TYPE(in_4), .WF_TYPE(in_8), .x_dout(Edata),
    .x_rok(Erok), .x_reqL(North_In_x_reql[1]), .in_ret(out_23), .x_reqN(Local_In_x_reqn[1]),
    .x_reqS(Local_In_x_reqs[2]), .x_reqW(Local_In_x_reqw[2]));  // open: x_reqE
  Xin South_In (
    .in_data(in_11), .FC_TYPE(in_9), .in_val(in_10), .x_gnt({WgntS, EgntS, NgntS, LgntS}), .x_Sidle(Sidle),
    .x_rd({Wrd, Erd, Nrd, Lrd}), .x_Eidle(Eidle), .x_Nidle(Nidle), .x_Lidle(Lidle), .x_Widle(Widle),
    .CLK(CLK), .RST(in_3), .ROUTING_TYPE(in_7), .FIFO_TYPE(in_4), .WF_TYPE(in_8), .x_dout(Sdata),
    .x_rok(Srok), .x_reqL(North_In_x_reql[2]), .in_ret(out_26), .x_reqN(Local_In_x_reqn[2]));  // open: x_reqE, x_reqS, x_reqW
  Xin West_In (
    .in_data(in_16), .FC_TYPE(in_9), .in_val(in_15), .x_gnt({1'b0, EgntW, 1'b0, LgntW}), .x_Sidle(Sidle),
    .x_rd({Srd, Erd, Nrd, Lrd}), .x_Eidle(Eidle), .x_Nidle(Nidle), .x_Lidle(Lidle), .x_Widle(Widle),
    .CLK(CLK), .RST(in_3), .ROUTING_TYPE(in_7), .FIFO_TYPE(in_4), .WF_TYPE(in_8), .x_dout(Wdata),
    .x_rok(Wrok), .x_reqL(North_In_x_reql[3]), .in_ret(out_29), .x_reqN(Local_In_x_reqn[3]),
    .x_reqE(Local_In_x_reqe[3]), .x_reqS(Local_In_x_reqs[3]));  // open: x_reqW
  Xout Local_Out (
    .x_req(North_In_x_reql), .CLK(CLK), .RST(in_3), .x_rok({Wrok, Srok, Erok, Nrok}), .x_din0(Ndata),
    .x_din1(Edata), .x_din2(Sdata), .x_din3(Wdata), .FIFO_TYPE(in_4), .out_ret(in_12), .FC_TYPE(in_9),
    .x_gnt({LgntW, LgntS, LgntE, LgntN}), .x_idle(Lidle), .out_data(out_18), .x_rd(Lrd), .out_val(out_19));
  Xout North_Out (
    .x_req(Local_In_x_reqn), .CLK(CLK), .RST(in_3), .x_rok({Wrok, Srok, Erok, Lrok}), .x_din0(Ldata),
    .x_din1(Edata), .x_din2(Sdata), .x_din3(Wdata), .FIFO_TYPE(in_4), .out_ret(in_12), .FC_TYPE(in_9),
    .x_gnt({NgntW, NgntS, NgntE, NgntL}), .x_idle(Nidle), .out_data(out_21), .x_rd(Nrd), .out_val(out_22));
  Xout East_Out (
    .x_req({Local_In_x_reqe[3], 2'b00, Local_In_x_reqe[0]}), .CLK(CLK), .RST(in_3),
    .x_rok({Wrok, Srok, Nrok, Lrok}), .x_din0(Ldata), .x_din1(Ndata), .x_din2(Sdata), .x_din3(Wdata),
    .FIFO_TYPE(in_4), .out_ret(in_12), .FC_TYPE(in_9), .x_gnt({EgntW, EgntS, EgntN, EgntL}), .x_idle(Eidle),
    .out_data(out_27), .x_rd(Erd), .out_val(out_25));
  Xout South_Out (
    .x_req(Local_In_x_reqs), .CLK(CLK), .RST(in_3), .x_rok({Wrok, Erok, Nrok, Lrok}), .x_din0(Ldata),
    .x_din1(Ndata), .x_din2(Edata), .x_din3(Wdata), .FIFO_TYPE(in_4), .out_ret(in_12), .FC_TYPE(in_9),
    .x_gnt({SgntW, SgntE, SgntN, SgntL}), .x_idle(Sidle), .out_data(out_24), .x_rd(Srd), .out_val(out_28));
  Xout Weast_Out (
    .x_req({1'b0, Local_In_x_reqw[2], 1'b0, Local_In_x_reqw[0]}), .CLK(CLK), .RST(in_3),
    .x_rok({Srok, Erok, Nrok, Lrok}), .x_din0(Ldata), .x_din1(Ndata), .x_din2(Edata), .x_din3(Sdata),
    .FIFO_TYPE(in_4), .out_ret(in_12), .FC_TYPE(in_9), .x_gnt({WgntS, WgntE, WgntN, WgntL}), .x_idle(Widle),
    .out_data(out_30), .x_rd(Wrd), .out_val(out_31));

  // Other names for the same wires on the sheet: East_in_data[9:0] = in_14; East_in_ret = out_23; East_In_val = in_13;
  //   East_out_data[9:0] = out_27; East_out_val = out_25; FC_TYPE = in_9; FIFO_TYPE = in_4; Local_in_data[9:0] = in_2;
  //   Local_in_ret = out_17; Local_In_val = in_1; Local_out_data[9:0] = out_18; Local_out_val = out_19;
  //   Nort_In_val = in_5; North_in_data[9:0] = in_6; North_in_ret = out_20; North_out_data[9:0] = out_21;
  //   North_out_val = out_22; Out_ret = in_12; ROUTING_TYPE = in_7; RST = in_3; South_in_data[9:0] = in_11;
  //   South_in_ret = out_26; South_In_val = in_10; South_out_data[9:0] = out_24; South_out_val = out_28;
  //   West_in_data[9:0] = in_16; West_in_ret = out_29; West_In_val = in_15; West_out_data[9:0] = out_30;
  //   West_out_val = out_31; WF_TYPE = in_8
endmodule

module routing_xy (
  input  bop,
  input  rok,
  input  [3:0] Xdest,
  input  [3:0] Ydest,
  output reqE,
  output reqW,
  output reqN,
  output reqS,
  output reqL
);

  wire and_1_out, comparator_1_eq, comparator_1_gt, comparator_1_lt, comparator_2_eq, comparator_2_gt,
       comparator_2_lt;

  and and_1 (and_1_out, bop, rok);
  Comparator #(.width(4)) comparator_1 (
    .a(Xdest), .b(4'b0011), .gt(comparator_1_gt), .eq(comparator_1_eq), .lt(comparator_1_lt));
  Comparator #(.width(4)) comparator_2 (
    .a(Ydest), .b(4'b0011), .gt(comparator_2_gt), .eq(comparator_2_eq), .lt(comparator_2_lt));
  and and_2 (reqE, and_1_out, comparator_1_gt);
  and and_3 (reqW, and_1_out, comparator_1_lt);
  and and_4 (reqN, comparator_1_eq, comparator_2_gt, and_1_out);
  and and_5 (reqS, and_1_out, comparator_1_eq, comparator_2_lt);
  and and_6 (reqL, comparator_2_eq, and_1_out, comparator_1_eq);

  // Notes on the sheet:
  //   XID
  //   YID
  //   header_present
endmodule

module routing_wf (
  input  bop,
  input  rok,
  input  WF_TYPE,
  input  [3:0] Xdest,
  input  [3:0] Ydest,
  input  Sidle,
  input  Eidle,
  input  Nidle,
  output reqW,
  output reqN,
  output reqL,
  output reqS,
  output reqE
);

  wire and_1_out, and_4_out, and_5_out, and_6_out, and_7_out, and_8_out, and_9_out, and_10_out, and_11_out,
       comparator_1_eq, comparator_1_gt, comparator_1_lt, comparator_2_eq, comparator_2_gt, comparator_2_lt,
       Diag_NE_out, Diag_SE_out, multiplexer_1_out, multiplexer_2_out, multiplexer_3_out, not_1_out,
       not_2_out, not_3_out, reqE_E_out, reqE_Y_out, reqN_E_out, reqN_Y_out, reqS_E_out, reqS_Y_out,
       Reto_E_out, Reto_N_out, Reto_S_out;

  not not_1 (not_1_out, Sidle);
  not not_2 (not_2_out, Eidle);
  not not_3 (not_3_out, Nidle);
  and Reto_N (Reto_N_out, comparator_2_gt, comparator_1_eq);
  and and_1 (and_1_out, bop, rok);
  Comparator #(.width(4)) comparator_1 (
    .a(Xdest), .b(4'b0011), .gt(comparator_1_gt), .eq(comparator_1_eq), .lt(comparator_1_lt));
  Comparator #(.width(4)) comparator_2 (
    .a(Ydest), .b(4'b0011), .gt(comparator_2_gt), .eq(comparator_2_eq), .lt(comparator_2_lt));
  and Reto_S (Reto_S_out, comparator_2_lt, comparator_1_eq);
  and Reto_E (Reto_E_out, comparator_2_eq, comparator_1_gt);
  and Diag_NE (Diag_NE_out, comparator_2_gt, comparator_1_gt);
  and Diag_SE (Diag_SE_out, comparator_1_gt, comparator_2_lt);
  and and_2 (reqW, and_1_out, comparator_1_lt);
  and and_3 (reqL, and_1_out, comparator_1_eq, comparator_2_eq);
  and and_4 (and_4_out, Diag_NE_out, Nidle);
  and and_5 (and_5_out, Diag_SE_out, Sidle);
  and and_6 (and_6_out, Diag_NE_out, not_3_out, Eidle);
  and and_7 (and_7_out, Diag_SE_out, Eidle, not_1_out);
  and and_8 (and_8_out, Diag_NE_out, Eidle);
  and and_9 (and_9_out, Diag_SE_out, Eidle);
  and and_10 (and_10_out, Diag_NE_out, Nidle, not_2_out);
  and and_11 (and_11_out, Diag_SE_out, Sidle, not_2_out);
  or reqN_Y (reqN_Y_out, and_4_out, Reto_N_out);
  or reqS_Y (reqS_Y_out, and_5_out, Reto_S_out);
  or reqE_Y (reqE_Y_out, and_6_out, Reto_E_out, and_7_out);
  or reqE_E (reqE_E_out, and_8_out, Reto_E_out, and_9_out);
  or reqN_E (reqN_E_out, and_10_out, Reto_N_out);
  or reqS_E (reqS_E_out, and_11_out, Reto_S_out);
  Multiplexer multiplexer_1 (.in0(reqN_Y_out), .in1(reqN_E_out), .out(multiplexer_1_out), .sel(WF_TYPE));
  Multiplexer multiplexer_2 (.in0(reqS_Y_out), .in1(reqS_E_out), .out(multiplexer_2_out), .sel(WF_TYPE));
  Multiplexer multiplexer_3 (.in0(reqE_Y_out), .in1(reqE_E_out), .out(multiplexer_3_out), .sel(WF_TYPE));
  and and_12 (reqN, multiplexer_1_out, and_1_out);
  and and_13 (reqS, multiplexer_2_out, and_1_out);
  and and_14 (reqE, multiplexer_3_out, and_1_out);

  // Notes on the sheet:
  //   XID
  //   YID
  //   header_present
endmodule

module arb_rr (
  input  [3:0] R,
  input  RST,
  input  CLK,
  output [3:0] G,
  output idle
);

  wire [3:0] pg_1_p;

  pg pg_1 (.G(G), .CLK(CLK), .RST(RST), .P(pg_1_p));
  ppe ppe_1 (.R(R), .P(pg_1_p), .CLK(CLK), .RST(RST), .G(G), .idle(idle));
endmodule

module pg (
  input  [3:0] G,
  input  CLK,
  input  RST,
  output [3:0] P
);

  wire or_1_out, or_2_out;
  wire [3:0] and_1_out, multiplexer_1_out, not_1_out, register_1_q;

  Register #(.width(4)) register_1 (.D(G), .en(1'b1), .clk(CLK), .Q(register_1_q), .clr(RST));
  assign not_1_out = ~register_1_q;  // NOT_Gate not_1, 4 bits wide
  assign and_1_out = G & not_1_out;  // AND_Gate and_1, 4 bits wide
  Multiplexer #(.width(4)) multiplexer_1 (.in0({G[2:0], G[3]}), .in1(4'b0001), .out(multiplexer_1_out), .sel(RST));
  or or_1 (or_1_out, or_2_out, RST);
  Register #(.width(4)) register_2 (.D(multiplexer_1_out), .en(or_1_out), .clk(CLK), .Q(P));  // open: clr
  or or_2 (or_2_out, and_1_out[0], and_1_out[1], and_1_out[2], and_1_out[3]);

  // Notes on the sheet:
  //   nextP
  //   Gdelayed
  //   granting
  //   update_register
endmodule

module ppe (
  input  [3:0] R,
  input  [3:0] P,
  input  CLK,
  input  RST,
  output [3:0] G,
  output idle
);

  wire and_1_out, and_2_out, and_3_out, and_4_out, and_5_out, and_6_out, and_7_out, and_8_out, and_9_out,
       and_10_out, and_11_out, and_12_out, not_1_out, not_2_out, not_3_out, not_4_out, not_5_out, not_6_out,
       not_7_out, not_8_out, or_1_out, or_2_out, or_3_out, or_4_out;
  wire [3:0] multiplexer_1_out;

  not not_1 (not_1_out, P[0]);
  not not_2 (not_2_out, P[1]);
  not not_3 (not_3_out, P[2]);
  not not_4 (not_4_out, P[3]);
  and and_1 (and_1_out, not_1_out, or_4_out);
  and and_2 (and_2_out, not_2_out, or_1_out);
  and and_3 (and_3_out, not_3_out, or_2_out);
  and and_4 (and_4_out, not_4_out, or_3_out);
  or or_1 (or_1_out, R[0], and_1_out);
  or or_2 (or_2_out, R[1], and_2_out);
  or or_3 (or_3_out, R[2], and_3_out);
  or or_4 (or_4_out, R[3], and_4_out);
  not not_5 (not_5_out, and_1_out);
  not not_6 (not_6_out, and_2_out);
  not not_7 (not_7_out, and_3_out);
  not not_8 (not_8_out, and_4_out);
  and and_5 (and_5_out, R[0], not_5_out);
  and and_6 (and_6_out, R[1], not_6_out);
  and and_7 (and_7_out, R[2], not_7_out);
  and and_8 (and_8_out, R[3], not_8_out);
  and and_9 (and_9_out, R[0], G[0]);
  and and_10 (and_10_out, R[1], G[1]);
  and and_11 (and_11_out, R[2], G[2]);
  and and_12 (and_12_out, R[3], G[3]);
  Register #(.width(4)) register_1 (.D(multiplexer_1_out), .en(1'b1), .clk(CLK), .Q(G), .clr(RST));
  Multiplexer multiplexer_1 (.in0(and_9_out), .in1(and_5_out), .out(multiplexer_1_out[0]), .sel(idle));
  Multiplexer multiplexer_2 (.in0(and_10_out), .in1(and_6_out), .out(multiplexer_1_out[1]), .sel(idle));
  Multiplexer multiplexer_3 (.in0(and_11_out), .in1(and_7_out), .out(multiplexer_1_out[2]), .sel(idle));
  Multiplexer multiplexer_4 (.in0(and_12_out), .in1(and_8_out), .out(multiplexer_1_out[3]), .sel(idle));
  nor nor_1 (idle, G[0], G[1], G[2], G[3]);

  // Notes on the sheet:
  //   Lock
  //   Lock
  //   Lock
  //   Lock
  //   Imed_out0
  //   Imed_out1
  //   Imed_out2
  //   Imed_out3
  //   Grant0
  //   Grant1
  //   Grant2
  //   Grant3
  //   s_idle
endmodule

module fifo_controller (
  input  CLK,
  input  RST,
  input  write_req,
  input  read_req,
  output [1:0] wr_addr,
  output full,
  output empty,
  output [1:0] rd_addr
);

  wire and_1_out, and_2_out, comparator_2_eq, not_1_out, not_2_out, xor_1_out;
  wire [2:0] adder_1_out, adder_2_out;
  wire [2:2] register_1_q, register_2_q;

  Register #(.width(3)) register_1 (
    .D(adder_1_out), .en(and_1_out), .clk(CLK), .Q({register_1_q[2], wr_addr}), .clr(RST));
  Register #(.width(3)) register_2 (
    .D(adder_2_out), .en(and_2_out), .clk(CLK), .Q({register_2_q[2], rd_addr}), .clr(RST));
  Adder #(.width(3)) adder_1 (.a({register_1_q[2], wr_addr}), .b(3'b001), .out(adder_1_out));  // open: cin, cout
  and and_1 (and_1_out, write_req, not_1_out);
  not not_1 (not_1_out, full);
  Adder #(.width(3)) adder_2 (.a({register_2_q[2], rd_addr}), .b(3'b001), .out(adder_2_out));  // open: cin, cout
  and and_2 (and_2_out, read_req, not_2_out);
  not not_2 (not_2_out, empty);
  Comparator #(.width(3)) comparator_1 (
    .a({register_1_q[2], wr_addr}), .b({register_2_q[2], rd_addr}), .eq(empty));  // open: gt, lt
  Comparator #(.width(2)) comparator_2 (.a(wr_addr), .b(rd_addr), .eq(comparator_2_eq));  // open: gt, lt
  xor xor_1 (xor_1_out, register_1_q[2], register_2_q[2]);
  and and_3 (full, comparator_2_eq, xor_1_out);
endmodule

module fifo (
  input  [9:0] din,
  input  CLK,
  input  RST,
  input  rd,
  input  wr,
  input  FIFO_TYPE,
  output [9:0] dout,
  output rok,
  output wok
);

  wire and_1_out, fifo_controller_1_empty, fifo_controller_1_full;
  wire [1:0] fifo_controller_1_rd_addr, fifo_controller_1_wr_addr;
  wire [9:0] fifo_datapath_ring_1_dout, fifo_datapath_shift_1_dout;

  and and_1 (and_1_out, wr, wok);
  fifo_controller fifo_controller_1 (
    .CLK(CLK), .RST(RST), .write_req(wr), .read_req(rd), .wr_addr(fifo_controller_1_wr_addr),
    .full(fifo_controller_1_full), .empty(fifo_controller_1_empty), .rd_addr(fifo_controller_1_rd_addr));
  not not_1 (rok, fifo_controller_1_empty);
  not not_2 (wok, fifo_controller_1_full);
  fifo_datapath_ring fifo_datapath_ring_1 (
    .din(din), .CLK(CLK), .RST(RST), .we(and_1_out), .wr_addr(fifo_controller_1_wr_addr),
    .rd_addr(fifo_controller_1_rd_addr), .dout(fifo_datapath_ring_1_dout));
  Multiplexer #(.width(10)) multiplexer_1 (
    .in0(fifo_datapath_ring_1_dout), .in1(fifo_datapath_shift_1_dout), .out(dout), .sel(FIFO_TYPE));
  fifo_datapath_shift fifo_datapath_shift_1 (
    .we(and_1_out), .din(din), .CLK(CLK), .RST(RST), .dout(fifo_datapath_shift_1_dout));
endmodule

module fifo_datapath_ring (
  input  [9:0] din,
  input  CLK,
  input  RST,
  input  we,
  input  [1:0] wr_addr,
  input  [1:0] rd_addr,
  output [9:0] dout
);

  wire demultiplexer_1_out0, demultiplexer_1_out1, demultiplexer_1_out2, demultiplexer_1_out3;
  wire [9:0] register_1_q, register_2_q, register_3_q, register_4_q;

  Register #(.width(10)) register_1 (.D(din), .en(demultiplexer_1_out0), .clk(CLK), .Q(register_1_q), .clr(RST));
  Register #(.width(10)) register_2 (.D(din), .en(demultiplexer_1_out1), .clk(CLK), .Q(register_2_q), .clr(RST));
  Register #(.width(10)) register_3 (.D(din), .en(demultiplexer_1_out2), .clk(CLK), .Q(register_3_q), .clr(RST));
  Register #(.width(10)) register_4 (.D(din), .en(demultiplexer_1_out3), .clk(CLK), .Q(register_4_q), .clr(RST));
  Demultiplexer #(.select(2)) demultiplexer_1 (
    .out0(demultiplexer_1_out0), .out1(demultiplexer_1_out1), .out2(demultiplexer_1_out2),
    .out3(demultiplexer_1_out3), .in(we), .sel(wr_addr));
  Multiplexer #(.select(2), .width(10)) multiplexer_1 (
    .in0(register_1_q), .in1(register_2_q), .in2(register_3_q), .in3(register_4_q), .out(dout), .sel(rd_addr));
endmodule

module fifo_datapath_shift (
  input  we,
  input  [9:0] din,
  input  CLK,
  input  RST,
  output [9:0] dout
);

  wire [9:0] register_1_q, register_2_q, register_3_q;

  Register #(.width(10)) register_1 (.D(din), .en(we), .clk(CLK), .Q(register_1_q), .clr(RST));
  Register #(.width(10)) register_2 (.D(register_1_q), .en(we), .clk(CLK), .Q(register_2_q), .clr(RST));
  Register #(.width(10)) register_3 (.D(register_2_q), .en(we), .clk(CLK), .Q(register_3_q), .clr(RST));
  Register #(.width(10)) register_4 (.D(register_3_q), .en(we), .clk(CLK), .Q(dout), .clr(RST));
endmodule

module cpm (
  input  [3:0] Lreq_in,
  input  [3:0] Lgnt_in,
  input  [3:0] Ereq_in,
  input  [3:0] Sgnt_in,
  input  [3:0] Wreq_in,
  input  [3:0] Ngnt_in,
  input  [3:0] Nreq_in,
  input  [3:0] Sreq_in,
  input  ROUTING_TYPE,
  input  [3:0] Egnt_in,
  input  [3:0] Wgnt_in,
  output [3:0] Lreq_out,
  output [3:0] Lgnt_out,
  output [3:0] Ereq_out,
  output [3:0] Sgnt_out,
  output [3:0] Wreq_out,
  output [3:0] Ngnt_out,
  output [3:0] Nreq_out,
  output [3:0] Sreq_out,
  output [3:0] Egnt_out,
  output [3:0] Wgnt_out
);

  and and_1 (Nreq_out[1], Nreq_in[1], ROUTING_TYPE);
  and and_2 (Sreq_out[2], Sreq_in[2], ROUTING_TYPE);
  and and_3 (Egnt_out[1], Egnt_in[1], ROUTING_TYPE);
  and and_4 (Egnt_out[2], Egnt_in[2], ROUTING_TYPE);

  assign {Egnt_out[3], Egnt_out[0]} = {Egnt_in[3], Egnt_in[0]};
  assign Ereq_out = Ereq_in;
  assign Lgnt_out = Lgnt_in;
  assign Lreq_out = Lreq_in;
  assign Ngnt_out = Ngnt_in;
  assign {Nreq_out[3:2], Nreq_out[0]} = {1'b0, Nreq_in[2], Nreq_in[0]};
  assign Sgnt_out = Sgnt_in;
  assign {Sreq_out[3], Sreq_out[1:0]} = {1'b0, Sreq_in[1:0]};
  assign Wgnt_out = {1'b0, Wgnt_in[2], 1'b0, Wgnt_in[0]};
  assign Wreq_out = Wreq_in;
endmodule

module ic (
  input  [3:0] Xdest,
  input  [3:0] Ydest,
  input  bop,
  input  rok,
  input  Sidle,
  input  Eidle,
  input  Nidle,
  input  ROUTING_TYPE,
  input  WF_TYPE,
  input  CLK,
  input  RST,
  input  Lidle,
  input  rd,
  input  Widle,
  input  eop,
  output reqL,
  output reqN,
  output reqE,
  output reqS,
  output reqW
);

  wire routing_wf_1_reqe, routing_wf_1_reql, routing_wf_1_reqn, routing_wf_1_reqs, routing_wf_1_reqw,
       routing_xy_1_reqe, routing_xy_1_reql, routing_xy_1_reqn, routing_xy_1_reqs, routing_xy_1_reqw;
  wire [4:0] multiplexer_1_out;

  routing_xy routing_xy_1 (
    .bop(bop), .rok(rok), .Xdest(Xdest), .Ydest(Ydest), .reqE(routing_xy_1_reqe), .reqW(routing_xy_1_reqw),
    .reqN(routing_xy_1_reqn), .reqS(routing_xy_1_reqs), .reqL(routing_xy_1_reql));
  routing_wf routing_wf_1 (
    .bop(bop), .rok(rok), .WF_TYPE(WF_TYPE), .Xdest(Xdest), .Ydest(Ydest), .Sidle(Sidle), .Eidle(Eidle),
    .Nidle(Nidle), .reqW(routing_wf_1_reqw), .reqN(routing_wf_1_reqn), .reqL(routing_wf_1_reql),
    .reqS(routing_wf_1_reqs), .reqE(routing_wf_1_reqe));
  Multiplexer multiplexer_1 (
    .in0(routing_xy_1_reql), .in1(routing_wf_1_reql), .out(multiplexer_1_out[0]), .sel(ROUTING_TYPE));
  Multiplexer multiplexer_2 (
    .in0(routing_xy_1_reqn), .in1(routing_wf_1_reqn), .out(multiplexer_1_out[1]), .sel(ROUTING_TYPE));
  Multiplexer multiplexer_3 (
    .in0(routing_xy_1_reqe), .in1(routing_wf_1_reqe), .out(multiplexer_1_out[2]), .sel(ROUTING_TYPE));
  Multiplexer multiplexer_4 (
    .in0(routing_xy_1_reqs), .in1(routing_wf_1_reqs), .out(multiplexer_1_out[3]), .sel(ROUTING_TYPE));
  Multiplexer multiplexer_5 (
    .in0(routing_xy_1_reqw), .in1(routing_wf_1_reqw), .out(multiplexer_1_out[4]), .sel(ROUTING_TYPE));
  req_reg req_reg_1 (
    .in_req(multiplexer_1_out), .CLK(CLK), .RST(RST), .rok(rok), .bop(bop), .rd(rd), .eop(eop),
    .out_req({reqW, reqS, reqE, reqN, reqL}));
endmodule

module req_reg (
  input  [4:0] in_req,
  input  CLK,
  input  RST,
  input  rok,
  input  bop,
  input  rd,
  input  eop,
  output [4:0] out_req
);

  wire and_1_out, and_2_out, not_1_out, or_1_out, or_2_out;

  and and_1 (and_1_out, rd, rok, eop);
  Register #(.width(5)) register_1 (.D(in_req), .en(and_2_out), .clk(CLK), .Q(out_req), .clr(or_1_out));
  and and_2 (and_2_out, rok, bop, not_1_out);
  or or_1 (or_1_out, RST, and_1_out);
  not not_1 (not_1_out, or_2_out);
  or or_2 (or_2_out, out_req[0], out_req[1], out_req[2], out_req[3], out_req[4]);
endmodule

module ifc (
  input  FC_TYPE,
  input  val,
  input  rd,
  input  rok,
  input  CLK,
  input  RST,
  input  wok,
  output wr,
  output ret
);

  wire and_1_out, d_ff_1_q, not_1_out, not_2_out, or_1_out;
  wire [1:0] and_2_out, register_1_q;

  and and_1 (and_1_out, rd, rok);
  and and_2 (and_2_out[0], val, wok, not_2_out, not_1_out);
  not not_1 (not_1_out, register_1_q[1]);
  not not_2 (not_2_out, register_1_q[0]);
  Multiplexer multiplexer_1 (.in0(val), .in1(register_1_q[0]), .out(wr), .sel(FC_TYPE));
  D_Flip_Flop d_ff_1 (.D(and_1_out), .clk(CLK), .Q(d_ff_1_q), .reset(RST));  // open: Qn, preset
  or or_1 (or_1_out, register_1_q[1], register_1_q[0]);
  Multiplexer multiplexer_2 (.in0(d_ff_1_q), .in1(or_1_out), .out(ret), .sel(FC_TYPE));
  and and_3 (and_2_out[1], or_1_out, val);
  Register #(.width(2)) register_1 (.D(and_2_out), .en(1'b1), .clk(CLK), .Q(register_1_q), .clr(RST));

  // Notes on the sheet:
  //   wr_credit
  //   ret_credit
  //   ret_handshake
  //   wr_handshake
endmodule

module irs (
  input  [3:0] sel,
  input  [3:0] rdin,
  output rdout
);

  wire and_1_out, and_2_out, and_3_out, and_4_out;

  and and_1 (and_1_out, sel[0], rdin[0]);
  and and_2 (and_2_out, sel[1], rdin[1]);
  and and_3 (and_3_out, sel[2], rdin[2]);
  and and_4 (and_4_out, sel[3], rdin[3]);
  or or_1 (rdout, and_1_out, and_2_out, and_3_out, and_4_out);
endmodule

module oc (
  input  [3:0] R,
  input  RST,
  input  CLK,
  output [3:0] G,
  output idle
);

  wire [3:0] arb_rr_1_g;

  arb_rr arb_rr_1 (.R(R), .RST(RST), .CLK(CLK), .G(arb_rr_1_g), .idle(idle));
  assign G = R & arb_rr_1_g;  // AND_Gate and_1, 4 bits wide
endmodule

module ods (
  input  [9:0] din0,
  input  [9:0] din1,
  input  [9:0] din2,
  input  [9:0] din3,
  input  [3:0] sel,
  output [9:0] dout
);

  wire [9:0] and_1_out, and_2_out, and_3_out, and_4_out, bit_extender_1_out, bit_extender_2_out,
       bit_extender_3_out, bit_extender_4_out;

  assign bit_extender_1_out = {{9{sel[0]}}, sel[0]};  // Bit_Extender bit_extender_1
  assign bit_extender_2_out = {{9{sel[1]}}, sel[1]};  // Bit_Extender bit_extender_2
  assign bit_extender_3_out = {{9{sel[2]}}, sel[2]};  // Bit_Extender bit_extender_3
  assign bit_extender_4_out = {{9{sel[3]}}, sel[3]};  // Bit_Extender bit_extender_4
  assign and_1_out = din0 & bit_extender_1_out;  // AND_Gate and_1, 10 bits wide
  assign and_2_out = din1 & bit_extender_2_out;  // AND_Gate and_2, 10 bits wide
  assign and_3_out = din2 & bit_extender_3_out;  // AND_Gate and_3, 10 bits wide
  assign and_4_out = din3 & bit_extender_4_out;  // AND_Gate and_4, 10 bits wide
  assign dout = and_1_out | and_2_out | and_3_out | and_4_out;  // OR_Gate or_1, 10 bits wide
endmodule

module ofc (
  input  ret,
  input  rok,
  input  RST,
  input  CLK,
  input  FC_TYPE,
  output val,
  output rd
);

  wire and_3_out, comparator_1_eq, Dec_out, Inc_out, not_1_out, not_2_out, not_3_out, not_4_out, or_1_out,
       or_2_out, or_3_out;
  wire [1:0] and_1_out, register_1_q;
  wire [2:0] counter_1_q;

  not not_1 (not_1_out, rok);
  not not_2 (not_2_out, ret);
  and Inc (Inc_out, ret, not_1_out);
  and Dec (Dec_out, not_2_out, rok);
  or or_1 (or_1_out, rok, register_1_q[0]);
  or or_2 (or_2_out, Inc_out, Dec_out);
  not not_3 (not_3_out, ret);
  and and_1 (and_1_out[0], not_3_out, or_1_out);
  and and_2 (and_1_out[1], register_1_q[0], ret);
  Counter #(.max('h4), .width(3)) counter_1 (
    .load(RST), .up(Inc_out), .count(or_2_out), .clk(CLK), .D(3'b100), .Q(counter_1_q));  // open: clr, carry
  Register #(.width(2)) register_1 (.D(and_1_out), .clk(CLK), .Q(register_1_q), .clr(RST));  // open: en
  Comparator #(.width(3)) comparator_1 (.a(counter_1_q), .b(3'b000), .eq(comparator_1_eq));  // open: gt, lt
  not not_4 (not_4_out, comparator_1_eq);
  or or_3 (or_3_out, ret, not_4_out);
  and and_3 (and_3_out, rok, or_3_out);
  Multiplexer multiplexer_1 (.in0(and_3_out), .in1(register_1_q[0]), .out(val), .sel(FC_TYPE));
  Multiplexer multiplexer_2 (.in0(and_3_out), .in1(register_1_q[1]), .out(rd), .sel(FC_TYPE));

  // Notes on the sheet:
  //   val_handshake
  //   rd_handshake
  //   val_credit
  //   rd_credit
endmodule

module ows (
  input  [3:0] sel,
  input  [3:0] wrin,
  output wrout
);

  wire and_1_out, and_2_out, and_3_out, and_4_out;

  and and_1 (and_1_out, sel[0], wrin[0]);
  and and_2 (and_2_out, sel[1], wrin[1]);
  and and_3 (and_3_out, sel[2], wrin[2]);
  and and_4 (and_4_out, sel[3], wrin[3]);
  or or_1 (wrout, and_1_out, and_2_out, and_3_out, and_4_out);
endmodule

module Xin (
  input  [9:0] in_data,
  input  FC_TYPE,
  input  in_val,
  input  [3:0] x_gnt,
  input  x_Sidle,
  input  [3:0] x_rd,
  input  x_Eidle,
  input  x_Nidle,
  input  x_Lidle,
  input  x_Widle,
  input  CLK,
  input  RST,
  input  ROUTING_TYPE,
  input  FIFO_TYPE,
  input  WF_TYPE,
  output [9:0] x_dout,
  output x_rok,
  output x_reqL,
  output in_ret,
  output x_reqN,
  output x_reqE,
  output x_reqS,
  output x_reqW
);

  wire fifo_1_wok, ifc_1_wr, irs_1_rdout;

  ifc ifc_1 (
    .FC_TYPE(FC_TYPE), .val(in_val), .rd(irs_1_rdout), .rok(x_rok), .CLK(CLK), .RST(RST), .wok(fifo_1_wok),
    .wr(ifc_1_wr), .ret(in_ret));
  irs irs_1 (.sel(x_gnt), .rdin(x_rd), .rdout(irs_1_rdout));
  fifo fifo_1 (
    .din(in_data), .CLK(CLK), .RST(RST), .rd(irs_1_rdout), .wr(ifc_1_wr), .FIFO_TYPE(FIFO_TYPE),
    .dout(x_dout), .rok(x_rok), .wok(fifo_1_wok));
  ic ic_1 (
    .Xdest(x_dout[7:4]), .Ydest(x_dout[3:0]), .bop(x_dout[8]), .rok(x_rok), .Sidle(x_Sidle), .Eidle(x_Eidle),
    .Nidle(x_Nidle), .ROUTING_TYPE(ROUTING_TYPE), .WF_TYPE(WF_TYPE), .CLK(CLK), .RST(RST), .Lidle(x_Lidle),
    .rd(irs_1_rdout), .Widle(x_Widle), .eop(x_dout[9]), .reqL(x_reqL), .reqN(x_reqN), .reqE(x_reqE),
    .reqS(x_reqS), .reqW(x_reqW));
endmodule

module Xout (
  input  [3:0] x_req,
  input  CLK,
  input  RST,
  input  [3:0] x_rok,
  input  [9:0] x_din0,
  input  [9:0] x_din1,
  input  [9:0] x_din2,
  input  [9:0] x_din3,
  input  FIFO_TYPE,
  input  out_ret,
  input  FC_TYPE,
  output [3:0] x_gnt,
  output x_idle,
  output [9:0] out_data,
  output x_rd,
  output out_val
);

  wire fifo_1_rok, ofc_1_rd, ows_1_wrout;
  wire [9:0] ods_1_dout;

  oc oc_1 (.R(x_req), .RST(RST), .CLK(CLK), .G(x_gnt), .idle(x_idle));
  ows ows_1 (.sel(x_gnt), .wrin(x_rok), .wrout(ows_1_wrout));
  ods ods_1 (.din0(x_din0), .din1(x_din1), .din2(x_din2), .din3(x_din3), .sel(x_gnt), .dout(ods_1_dout));
  fifo fifo_1 (
    .din(ods_1_dout), .CLK(CLK), .RST(RST), .rd(ofc_1_rd), .wr(ows_1_wrout), .FIFO_TYPE(FIFO_TYPE),
    .dout(out_data), .rok(fifo_1_rok), .wok(x_rd));
  ofc ofc_1 (.ret(out_ret), .rok(fifo_1_rok), .RST(RST), .CLK(CLK), .FC_TYPE(FC_TYPE), .val(out_val), .rd(ofc_1_rd));
endmodule
