// Logisim project sdhsaidashd.circ as structural Verilog
module main (
  input  [3:0] G,
  input  CLK,
  input  RST,
  output [3:0] P
);

  wire or_1_out;
  wire [3:0] and_1_out, multiplexer_1_out, not_1_out, register_1_q;

  Register #(.width(4)) register_1 (.D(G), .clk(CLK), .Q(register_1_q));  // open: en, clr
  assign not_1_out = ~register_1_q;  // NOT_Gate not_1, 4 bits wide
  assign and_1_out = G & not_1_out;  // AND_Gate and_1, 4 bits wide
  Multiplexer #(.width(4)) multiplexer_1 (.in0({G[2:0], G[3]}), .in1(4'b0001), .out(multiplexer_1_out), .sel(RST));
  Register #(.width(4)) register_2 (.D(multiplexer_1_out), .clk(CLK));  // open: en, Q, clr
  or or_1 (or_1_out, and_1_out[0], and_1_out[1], and_1_out[2], and_1_out[3]);

  // Notes on the sheet:
  //   nextP
  //   Gdelayed
  //   granting
  //   update_register
endmodule
